# Fritzing sketch H-bridge (saved by Fritzing 0.7.11b)
breadboards: 1

parts:
  IC1 = L293D [package=THT]
  M1 = DC Motor
  Arduino1 = Arduino

nets:
  N1: IC1.Enable_1, Arduino1.D8
  N2: IC1.In_1, Arduino1.D7
  N3: IC1.Out_1_(_Controlled_by_Enable_1_), M1.pin_1
  N4: IC1.0V, Arduino1.GND
  N5: IC1.Out_2_(_Controlled_by_Enable_1_), M1.pin_2
  N6: IC1.In_2, Arduino1.D6
  N7: IC1.+Vmotor, IC1.+V, Arduino1.+5V
