# Fritzing sketch RGB (saved by Fritzing 0.7.11b)
breadboards: 1

parts:
  LED1 = RGB LED (com. anode, rbg) [package="5 mm [THT]"]
  Arduino1 = Arduino
  R1 = Resistor [tolerance=±5% resistance=150 package=THT]  # not connected
  R2 = Resistor [tolerance=±5% resistance=90 package=THT]
  R3 = Resistor [tolerance=±5% resistance=90 package=THT]

nets:
  N1: LED1.common_anode, Arduino1.GND
  N2: LED1.blue_cathode, R2.Pin_1
  N3: LED1.green_cathode, R3.Pin_1
  N4: Arduino1.D10, R2.Pin_0
  N5: Arduino1.D9, R3.Pin_0
