# Fritzing sketch RGB_pot (saved by Fritzing 0.7.11b)
breadboards: 1

parts:
  LED1 = RGB LED (com. cathode, rbg) [package="5 mm [THT]"]
  Arduino1 = Arduino
  R1 = Rotary Potentiometer (Small) [maximum_resistance=100kΩ]

nets:
  N1: LED1.red_anode, Arduino1.D11
  N2: LED1.common_cathode, Arduino1.GND, R1.leg1
  N3: LED1.blue_anode, Arduino1.D10
  N4: LED1.green_anode, Arduino1.D9
  N5: Arduino1.+5V, R1.leg2
  N6: Arduino1.A0, R1.wiper
