# Fritzing sketch SMA (saved by Fritzing 0.7.11b)
breadboards: 1

parts:
  IC1 = IC, DIP package, 6 pins [chip_label=IC]
  Arduino1 = Arduino
  R1 = Resistor [tolerance=±5% resistance=220 package=THT]
  L1 = Inductor [package="400 mil [THT]"]
  VCC1 = Battery
  S1 = Pushbutton [package="[THT]"]
  R2 = Resistor [tolerance=±5% resistance=220 package=THT]

nets:
  N1: IC1.pin1, Arduino1.D11, R1.Pin_1
  N2: IC1.pin3, Arduino1.GND, R1.Pin_0, VCC1.-, R2.Pin_0
  N3: IC1.pin5, L1.pin_0
  N4: Arduino1.D2, S1.Pin_3, S1.Pin_4, R2.Pin_1
  N5: Arduino1.+5V, S1.Pin_1, S1.Pin_2
  N6: L1.pin_1, VCC1.+
