# Fritzing sketch SMA_IRLB8743 (saved by Fritzing 0.7.11b)
breadboards: 1

parts:
  Arduino1 = Arduino
  R1 = Resistor [tolerance=±5% resistance=220 package=THT]
  L1 = Inductor [package="400 mil [THT]"]
  VCC1 = Battery
  S1 = Pushbutton [package="[THT]"]
  R2 = Resistor [tolerance=±5% resistance=220 package=THT]
  Q1 = Basic FET N-Channel [package="TO220 [THT]"]

nets:
  N1: Arduino1.GND, R1.Pin_0, VCC1.-, R2.Pin_0, Q1.source
  N2: Arduino1.D11, R1.Pin_1, Q1.gate
  N3: Arduino1.D2, S1.Pin_3, S1.Pin_4, R2.Pin_1
  N4: Arduino1.+5V, S1.Pin_1, S1.Pin_2
  N5: L1.pin_0, Q1.drain
  N6: L1.pin_1, VCC1.+
