# Fritzing sketch SMA_IRLB8743_12V_photocell (saved by Fritzing 0.7.11b)
breadboards: 1

parts:
  Arduino1 = Arduino
  R1 = Resistor [tolerance=±5% resistance=220 package=THT]
  L1 = Inductor [package="400 mil [THT]"]
  R2 = Resistor [tolerance=±5% resistance=220 package=THT]
  Q1 = Basic FET N-Channel [package="TO220 [THT]"]
  R3 = Photocell (LDR) [package=THT]

nets:
  N1: Arduino1.GND, R1.Pin_0, Q1.source, R3.pin_1
  N2: Arduino1.D11, R1.Pin_1, Q1.gate
  N3: Arduino1.+5V, R2.Pin_1
  N4: Arduino1.VIN, L1.pin_1
  N5: Arduino1.A0, R2.Pin_0, R3.pin_0
  N6: L1.pin_0, Q1.drain
