# Fritzing sketch pushButton_photocell (saved by Fritzing 0.7.11b)
breadboards: 1

parts:
  R1 = Resistor [tolerance=±5% resistance=220 package=THT]
  R2 = Resistor [tolerance=±5% resistance=220 package=THT]
  S1 = Pushbutton [package="[THT]"]
  R3 = Photocell (LDR) [package=THT]
  Arduino1 = Arduino

nets:
  N1: R1.Pin_0, S1.Pin_1, S1.Pin_2, Arduino1.D9
  N2: R1.Pin_1, R3.pin_0, Arduino1.GND
  N3: R2.Pin_0, R3.pin_1, Arduino1.A0
  N4: R2.Pin_1, S1.Pin_3, S1.Pin_4, Arduino1.+5V
