# Fritzing sketch tilt (saved by Fritzing 0.7.11b)
breadboards: 1

parts:
  Arduino1 = Arduino
  S1 = Tilt Switch [package=THT]
  R1 = Resistor [tolerance=±5% resistance=220 package=THT]

nets:
  N1: Arduino1.GND, R1.Pin_1
  N2: Arduino1.D2, S1.Pin_2, R1.Pin_0
  N3: Arduino1.+5V, S1.Pin_1
