# Fritzing sketch transistor_motor_vin (saved by Fritzing 0.7.11b)
breadboards: 1

parts:
  M1 = DC Motor
  Arduino1 = Arduino
  D1 = Rectifier Diode [part_number=1N4001 package="300 mil [THT]"]
  Q1 = npn-Powertransistor [package="TO220 [THT]"]
  R1 = Resistor [tolerance=±5% resistance=220 package=THT]
  S1 = Pushbutton [package="[THT]"]
  R2 = Resistor [tolerance=±5% resistance=220 package=THT]

nets:
  N1: M1.pin_1, Arduino1.+5V, D1.cathode, R2.Pin_1
  N2: M1.pin_2, D1.anode, Q1.collector
  N3: Arduino1.GND, Q1.emitter, R1.Pin_0, S1.Pin_3, S1.Pin_4
  N4: Arduino1.D9, S1.Pin_1, S1.Pin_2, R2.Pin_0
  N5: Arduino1.D7, Q1.base, R1.Pin_1
