# Fritzing sketch charlieplex (saved by Fritzing 0.7.11b)
breadboards: 1

parts:
  LED1 = LED - 5mm [color="Blue (470nm)" package="5 mm [THT]"]
  LED2 = LED - 5mm [color="Green (560nm)" package="5 mm [THT]"]
  LED3 = LED - 5mm [color="Yellow (595nm)" package="5 mm [THT]"]
  LED4 = LED - 5mm [color="Red (633nm)" package="5 mm [THT]"]
  Arduino1 = Arduino

nets:
  N1: LED1.cathode, LED3.cathode, Arduino1.D5
  N2: LED1.anode, LED2.anode, Arduino1.D3
  N3: LED2.cathode, LED4.cathode, Arduino1.D4
  N4: LED3.anode, LED4.anode, Arduino1.D2
